# Fritzing sketch board v1 (saved by Fritzing 0.9.10b)
perfboards: 2

parts:
  Debug_Button = Pushbutton [package="[SMD]"]
  I2S_-_Lock_Sensor = JST XH 4A 2.54mm [package=THT]
  I2S_-_Monitor = JST XH 4A 2.54mm [package=THT]
  WeMos_D1_Mini1 = WeMos D1 Mini
  J1 = male pin header, 2 pins [form="♂ (male)"]
  J2 = male pin header, 3 pins [form="♂ (male)"]
  R1 = Resistor [tolerance=±5% power=0.25 resistance=10k package=THT]
  Indoor_Buzzer = Passive Buzzer
  Outdoor_Buzzer = Passive Buzzer
  LED1 = smd LED [color="Red (633nm)" package="1206 [SMD]"]
  LED2 = LED - 5mm [color="Green (565nm)" current=0.030 package="5 mm [THT]"]
  LED3 = LED - 5mm [color="Green (565nm)" current=0.030 package="5 mm [THT]"]
  LED4 = smd LED [color="Red (633nm)" package="1206 [SMD]"]
  R2 = Resistor [tolerance=±5% power=0.25 resistance=220 package=THT]
  R3 = Resistor [tolerance=±5% power=0.25 resistance=220 package=THT]
  R4 = Resistor [tolerance=±5% power=0.25 resistance=220 package=THT]
  R5 = Resistor [tolerance=±5% power=0.25 resistance=220 package=THT]
  External_Module = JST XH 5A
  U2 = JST XH 5A
  J3 = male pin header, 3 pins [form="♂ (male)"]

nets:
  N1: Debug_Button.Pin_1, Debug_Button.Pin_2
  N2: Debug_Button.Pin_3, Debug_Button.Pin_4, WeMos_D1_Mini1.D8
  N3: I2S_-_Lock_Sensor.pin1, I2S_-_Monitor.pin1, WeMos_D1_Mini1.G
  N4: I2S_-_Lock_Sensor.pin2, I2S_-_Monitor.pin2, WeMos_D1_Mini1.3V3, J1.pin1, J2.pin3, Indoor_Buzzer.NC
  N5: I2S_-_Lock_Sensor.pin3, I2S_-_Monitor.pin3, WeMos_D1_Mini1.D1
  N6: I2S_-_Lock_Sensor.pin4, I2S_-_Monitor.pin4, WeMos_D1_Mini1.D2
  N7: WeMos_D1_Mini1.A0, J1.pin2, R1.Pin_0
  N8: WeMos_D1_Mini1.D0, J2.pin1, Indoor_Buzzer.S
  N9: J2.pin2, Indoor_Buzzer.-, External_Module.pin2
  N10: Outdoor_Buzzer.S, U2.pin3, J3.pin2
  N11: Outdoor_Buzzer.NC, U2.pin1, J3.pin1
  N12: Outdoor_Buzzer.-, U2.pin2, J3.pin3
  N13: LED1.cathode, LED4.cathode
  N14: LED1.anode, R5.Pin_1
  N15: LED2.cathode, LED3.cathode
  N16: LED2.anode, R2.Pin_0
  N17: LED3.anode, R3.Pin_1
  N18: LED4.anode, R4.Pin_0
  N19: R2.Pin_1, R3.Pin_0
  N20: R4.Pin_1, R5.Pin_0, U2.pin5

notes:
  door_lock v1.1

custom parts:
  JST XH 4A 2.54mm: 4 Pin JST XH connector
  JST XH 5A: JST XH 5A 2.54.mm
